# Fritzing sketch lora (saved by Fritzing 0.9.3b)

parts:
  Part1 = BluePill
  LoRa_Module1 = Ra-01 - LoRa Module SX1278 [part_number=SX1278]
  Part2 = Adafruit FTDI Friend [part_number="Adafruit #284"]

nets:
  N1: Part1.A4, LoRa_Module1.NSS
  N2: Part1.A5, LoRa_Module1.SCK
  N3: Part1.A6, LoRa_Module1.MISO
  N4: Part1.A7, LoRa_Module1.MOSI
  N5: Part1.B0, LoRa_Module1.RESET
  3V3: Part1.3V3, LoRa_Module1.3.3V
  GND: Part1.GND, LoRa_Module1.GND
  N6: Part1.3V31, Part2.VCC
  GND3: Part1.GND3, Part2.GND
  N7: Part1.A10, Part2.TX
  N8: Part1.A9, Part2.RX

custom parts:
  Ra-01 - LoRa Module SX1278: The Ra-01 LoRa Module featuring the SX1278 engine by Semtech. Module by AI-Thinker. Module (Ra-01) specifications from: https://www.banggood.com/Ra-01-Smart-Electronics-SX1278-LoRa-Spread-Spectrum-Wireless-Module-Ultra-Far-10KM-433M-p-1130769.html Description: Power supply: DC1.8-3.7V(3.3V) Chip: SX1278 Frequency: 433Mhz Operating temperature: -40~+85°C On Sheild Description (may vary by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
  Adafruit FTDI Friend: Long gone are the days of parallel ports and serial ports. Now the USB port reigns supreme! But USB is hard, and you just want to transfer your every-day serial data from a microcontroller to computer. What now? Enter the FTDI Friend! The FTDI Friend is a tweaked out FTDI FT232RL chip adapter. Sure, like the well-known FTDI cable, it can provide power to your project and there are 4 signal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
